// Logisim project PC2.circ as structural Verilog: 18 circuits, main circuit main
module main (
);

  wire alu_1_zero, CLK, cu_1_alusrc, cu_1_branch, cu_1_memread, cu_1_memtoreg, cu_1_memwrite, cu_1_regdst,
       cu_1_regwrite, Reset;
  wire [1:0] and_1_out, cu_1_aluop;
  wire [3:0] alu_control_1_operation;
  wire [4:0] instruction_decoder_1_rd, instruction_decoder_1_rs, instruction_decoder_1_rt, multiplexer_2_out;
  wire [5:0] driver0, driver1, driver2, driver3, driver4, driver5, driver6, driver7, driver8, driver9,
       driver10, drivera, driverb, driverc, driverd, drivere, driverf, Funct, Opcode;
  wire [6:0] display_driver_1_col0, display_driver_1_col1, display_driver_1_col2, display_driver_1_col3,
       display_driver_1_col4, display_driver_2_col0, display_driver_2_col1, display_driver_2_col2,
       display_driver_2_col3, display_driver_2_col4, display_driver_3_col0, display_driver_3_col1,
       display_driver_3_col2, display_driver_3_col3, display_driver_3_col4, display_driver_4_col0,
       display_driver_4_col1, display_driver_4_col2, display_driver_4_col3, display_driver_4_col4,
       display_driver_5_col0, display_driver_5_col1, display_driver_5_col2, display_driver_5_col3,
       display_driver_5_col4, display_driver_6_col0, display_driver_6_col1, display_driver_6_col2,
       display_driver_6_col3, display_driver_6_col4, display_driver_7_col0, display_driver_7_col1,
       display_driver_7_col2, display_driver_7_col3, display_driver_7_col4, display_driver_8_col0,
       display_driver_8_col1, display_driver_8_col2, display_driver_8_col3, display_driver_8_col4,
       display_driver_9_col0, display_driver_9_col1, display_driver_9_col2, display_driver_9_col3,
       display_driver_9_col4, display_driver_10_col0, display_driver_10_col1, display_driver_10_col2,
       display_driver_10_col3, display_driver_10_col4, display_driver_11_col0, display_driver_11_col1,
       display_driver_11_col2, display_driver_11_col3, display_driver_11_col4, display_driver_12_col0,
       display_driver_12_col1, display_driver_12_col2, display_driver_12_col3, display_driver_12_col4,
       display_driver_13_col0, display_driver_13_col1, display_driver_13_col2, display_driver_13_col3,
       display_driver_13_col4, display_driver_14_col0, display_driver_14_col1, display_driver_14_col2,
       display_driver_14_col3, display_driver_14_col4, display_driver_15_col0, display_driver_15_col1,
       display_driver_15_col2, display_driver_15_col3, display_driver_15_col4, display_driver_16_col0,
       display_driver_16_col1, display_driver_16_col2, display_driver_16_col3, display_driver_16_col4,
       display_driver_17_col0, display_driver_17_col1, display_driver_17_col2, display_driver_17_col3,
       display_driver_17_col4;
  wire [15:0] imm;
  wire [23:0] bit_extender_5_out, PC;
  wire [25:0] Inst;
  wire [31:0] adder_1_out, adder_2_out, alu_1_out_4, bit_extender_2_out, bit_extender_3_out,
       bit_extender_4_out, Curr_Inst, multiplexer_1_out, multiplexer_3_out, multiplexer_4_out,
       multiplexer_5_out, ram_2_data, register_1_q, register_memory_1_busa, register_memory_1_busb,
       subtractor_1_out;

  Clock clock_1 (.out(CLK));
  Button button_1 (.out(Reset));
  // Probe on PC
  Register #(.width(32)) register_1 (.D(multiplexer_3_out), .en(1'b1), .Q(register_1_q), .clk(CLK), .clr(Reset));
  // Probe on Curr_Inst
  // Probe on Opcode
  // Probe on Funct
  // Probe on Inst
  Adder #(.width(32)) adder_1 (.a(32'h1), .b(register_1_q), .out(adder_1_out));  // open: cin, cout
  Bit_Extender #(.in_width(32), .out_width(24)) bit_extender_1 (.in(register_1_q), .out(PC));
  assign bit_extender_2_out = {{17{1'b0}}, imm[14:0]};  // Bit_Extender bit_extender_2
  RAM #(.addrWidth(24), .dataWidth(32)) ram_1 (
    .addr(PC), .data(Curr_Inst), .sel(1'b1), .clk(CLK), .ld(1'b1), .clr(1'b0));
  Debug_Circuit debug_circuit_1 (
    .Funct(Funct), .Opcode(Opcode), .inst3(driver3), .inst2(driver2), .inst1(driver1), .inst0(driver0),
    .Inst(Inst), .disp0(driver4), .disp1(driver5), .disp2(driver6), .disp3(driver7), .disp4(driver8),
    .disp5(driver9), .disp6(drivera), .disp7(driverb), .disp8(driverc), .disp9(driverd), .disp10(drivere),
    .disp11(driverf), .disp12(driver10));
  Adder #(.width(32)) adder_2 (.a(adder_1_out), .b(bit_extender_2_out), .out(adder_2_out));  // open: cin, cout
  Subtractor #(.width(32)) subtractor_1 (
    .a(bit_extender_2_out), .b(adder_1_out), .out(subtractor_1_out));  // open: bin, bout
  Multiplexer #(.width(32), .enable("false")) multiplexer_1 (
    .in0(adder_2_out), .in1(subtractor_1_out), .out(multiplexer_1_out), .sel(imm[15]));
  DotMatrix dotmatrix_1 (
    .col0(display_driver_1_col0), .col1(display_driver_1_col1), .col2(display_driver_1_col2),
    .col3(display_driver_1_col3), .col4(display_driver_1_col4));
  Display_Driver display_driver_1 (
    .col0(display_driver_1_col0), .col1(display_driver_1_col1), .col2(display_driver_1_col2),
    .col3(display_driver_1_col3), .col4(display_driver_1_col4), .in_1(driver0));
  DotMatrix dotmatrix_2 (
    .col0(display_driver_3_col0), .col1(display_driver_3_col1), .col2(display_driver_3_col2),
    .col3(display_driver_3_col3), .col4(display_driver_3_col4));
  DotMatrix dotmatrix_3 (
    .col0(display_driver_2_col0), .col1(display_driver_2_col1), .col2(display_driver_2_col2),
    .col3(display_driver_2_col3), .col4(display_driver_2_col4));
  Display_Driver display_driver_2 (
    .col0(display_driver_2_col0), .col1(display_driver_2_col1), .col2(display_driver_2_col2),
    .col3(display_driver_2_col3), .col4(display_driver_2_col4), .in_1(driver2));
  Display_Driver display_driver_3 (
    .col0(display_driver_3_col0), .col1(display_driver_3_col1), .col2(display_driver_3_col2),
    .col3(display_driver_3_col3), .col4(display_driver_3_col4), .in_1(driver1));
  Instruction_Decoder instruction_decoder_1 (
    .Inst(Curr_Inst), .Opcode(Opcode), .rs(instruction_decoder_1_rs), .rt(instruction_decoder_1_rt),
    .rd(instruction_decoder_1_rd), .funct(Funct), .Immediate(imm), .address(Inst));  // open: shamt
  DotMatrix dotmatrix_4 (
    .col0(display_driver_4_col0), .col1(display_driver_4_col1), .col2(display_driver_4_col2),
    .col3(display_driver_4_col3), .col4(display_driver_4_col4));
  Display_Driver display_driver_4 (
    .col0(display_driver_4_col0), .col1(display_driver_4_col1), .col2(display_driver_4_col2),
    .col3(display_driver_4_col3), .col4(display_driver_4_col4), .in_1(driver3));
  assign bit_extender_3_out = {{6{1'b0}}, Inst};  // Bit_Extender bit_extender_3
  assign bit_extender_4_out = {{16{1'b0}}, imm};  // Bit_Extender bit_extender_4
  DotMatrix dotmatrix_5 (
    .col0(display_driver_7_col0), .col1(display_driver_7_col1), .col2(display_driver_7_col2),
    .col3(display_driver_7_col3), .col4(display_driver_7_col4));
  DotMatrix dotmatrix_6 (
    .col0(display_driver_5_col0), .col1(display_driver_5_col1), .col2(display_driver_5_col2),
    .col3(display_driver_5_col3), .col4(display_driver_5_col4));
  Display_Driver display_driver_5 (
    .col0(display_driver_5_col0), .col1(display_driver_5_col1), .col2(display_driver_5_col2),
    .col3(display_driver_5_col3), .col4(display_driver_5_col4), .in_1(driver4));
  Multiplexer #(.width(5), .enable("false")) multiplexer_2 (
    .in0(instruction_decoder_1_rt), .in1(instruction_decoder_1_rd), .out(multiplexer_2_out), .sel(cu_1_regdst));
  DotMatrix dotmatrix_7 (
    .col0(display_driver_6_col0), .col1(display_driver_6_col1), .col2(display_driver_6_col2),
    .col3(display_driver_6_col3), .col4(display_driver_6_col4));
  Display_Driver display_driver_6 (
    .col0(display_driver_6_col0), .col1(display_driver_6_col1), .col2(display_driver_6_col2),
    .col3(display_driver_6_col3), .col4(display_driver_6_col4), .in_1(driver6));
  Display_Driver display_driver_7 (
    .col0(display_driver_7_col0), .col1(display_driver_7_col1), .col2(display_driver_7_col2),
    .col3(display_driver_7_col3), .col4(display_driver_7_col4), .in_1(driver5));
  Multiplexer #(.select(2), .width(32), .enable("false")) multiplexer_3 (
    .in0(adder_1_out), .in1(multiplexer_1_out), .in2(bit_extender_3_out), .out(multiplexer_3_out),
    .sel(and_1_out));  // open: in3
  CU cu_1 (
    .Opcode(Opcode), .Jump(and_1_out[1]), .RegDst(cu_1_regdst), .ALUSrc(cu_1_alusrc),
    .MemToReg(cu_1_memtoreg), .RegWrite(cu_1_regwrite), .MemRead(cu_1_memread), .MemWrite(cu_1_memwrite),
    .Branch(cu_1_branch), .ALUOp(cu_1_aluop));  // open: DataBus
  Register_Memory register_memory_1 (
    .Data_in(multiplexer_4_out), .Write_Enable(cu_1_regwrite), .Clk(CLK), .Clear_Reset(Reset),
    .regA(instruction_decoder_1_rs), .RegB(instruction_decoder_1_rt), .RegC(multiplexer_2_out),
    .BusB(register_memory_1_busb), .BusA(register_memory_1_busa));
  DotMatrix dotmatrix_8 (
    .col0(display_driver_9_col0), .col1(display_driver_9_col1), .col2(display_driver_9_col2),
    .col3(display_driver_9_col3), .col4(display_driver_9_col4));
  DotMatrix dotmatrix_9 (
    .col0(display_driver_8_col0), .col1(display_driver_8_col1), .col2(display_driver_8_col2),
    .col3(display_driver_8_col3), .col4(display_driver_8_col4));
  Display_Driver display_driver_8 (
    .col0(display_driver_8_col0), .col1(display_driver_8_col1), .col2(display_driver_8_col2),
    .col3(display_driver_8_col3), .col4(display_driver_8_col4), .in_1(driver7));
  Display_Driver display_driver_9 (
    .col0(display_driver_9_col0), .col1(display_driver_9_col1), .col2(display_driver_9_col2),
    .col3(display_driver_9_col3), .col4(display_driver_9_col4), .in_1(driver8));
  DotMatrix dotmatrix_10 (
    .col0(display_driver_11_col0), .col1(display_driver_11_col1), .col2(display_driver_11_col2),
    .col3(display_driver_11_col3), .col4(display_driver_11_col4));
  DotMatrix dotmatrix_11 (
    .col0(display_driver_10_col0), .col1(display_driver_10_col1), .col2(display_driver_10_col2),
    .col3(display_driver_10_col3), .col4(display_driver_10_col4));
  Display_Driver display_driver_10 (
    .col0(display_driver_10_col0), .col1(display_driver_10_col1), .col2(display_driver_10_col2),
    .col3(display_driver_10_col3), .col4(display_driver_10_col4), .in_1(driver9));
  DotMatrix dotmatrix_12 (
    .col0(display_driver_12_col0), .col1(display_driver_12_col1), .col2(display_driver_12_col2),
    .col3(display_driver_12_col3), .col4(display_driver_12_col4));
  Display_Driver display_driver_11 (
    .col0(display_driver_11_col0), .col1(display_driver_11_col1), .col2(display_driver_11_col2),
    .col3(display_driver_11_col3), .col4(display_driver_11_col4), .in_1(drivera));
  Display_Driver display_driver_12 (
    .col0(display_driver_12_col0), .col1(display_driver_12_col1), .col2(display_driver_12_col2),
    .col3(display_driver_12_col3), .col4(display_driver_12_col4), .in_1(driverb));
  DotMatrix dotmatrix_13 (
    .col0(display_driver_13_col0), .col1(display_driver_13_col1), .col2(display_driver_13_col2),
    .col3(display_driver_13_col3), .col4(display_driver_13_col4));
  DotMatrix dotmatrix_14 (
    .col0(display_driver_15_col0), .col1(display_driver_15_col1), .col2(display_driver_15_col2),
    .col3(display_driver_15_col3), .col4(display_driver_15_col4));
  Display_Driver display_driver_13 (
    .col0(display_driver_13_col0), .col1(display_driver_13_col1), .col2(display_driver_13_col2),
    .col3(display_driver_13_col3), .col4(display_driver_13_col4), .in_1(driverc));
  DotMatrix dotmatrix_15 (
    .col0(display_driver_14_col0), .col1(display_driver_14_col1), .col2(display_driver_14_col2),
    .col3(display_driver_14_col3), .col4(display_driver_14_col4));
  Display_Driver display_driver_14 (
    .col0(display_driver_14_col0), .col1(display_driver_14_col1), .col2(display_driver_14_col2),
    .col3(display_driver_14_col3), .col4(display_driver_14_col4), .in_1(drivere));
  Display_Driver display_driver_15 (
    .col0(display_driver_15_col0), .col1(display_driver_15_col1), .col2(display_driver_15_col2),
    .col3(display_driver_15_col3), .col4(display_driver_15_col4), .in_1(driverd));
  Multiplexer #(.width(32), .enable("false")) multiplexer_4 (
    .in0(alu_1_out_4), .in1(ram_2_data), .out(multiplexer_4_out), .sel(cu_1_memtoreg));
  Multiplexer #(.width(32), .enable("false")) multiplexer_5 (
    .in0(register_memory_1_busa), .in1(bit_extender_4_out), .out(multiplexer_5_out), .sel(cu_1_alusrc));
  ALU_Control alu_control_1 (.ALUOp(cu_1_aluop), .Funct(Funct), .Operation(alu_control_1_operation));
  DotMatrix dotmatrix_16 (
    .col0(display_driver_17_col0), .col1(display_driver_17_col1), .col2(display_driver_17_col2),
    .col3(display_driver_17_col3), .col4(display_driver_17_col4));
  DotMatrix dotmatrix_17 (
    .col0(display_driver_16_col0), .col1(display_driver_16_col1), .col2(display_driver_16_col2),
    .col3(display_driver_16_col3), .col4(display_driver_16_col4));
  Display_Driver display_driver_16 (
    .col0(display_driver_16_col0), .col1(display_driver_16_col1), .col2(display_driver_16_col2),
    .col3(display_driver_16_col3), .col4(display_driver_16_col4), .in_1(driver10));
  Display_Driver display_driver_17 (
    .col0(display_driver_17_col0), .col1(display_driver_17_col1), .col2(display_driver_17_col2),
    .col3(display_driver_17_col3), .col4(display_driver_17_col4), .in_1(driverf));
  and and_1 (and_1_out[0], cu_1_branch, alu_1_zero);
  ALU alu_1 (
    .Input_A(register_memory_1_busb), .Input_B(multiplexer_5_out), .ALUOp(alu_control_1_operation),
    .out_4(alu_1_out_4), .Zero(alu_1_zero));
  Bit_Extender #(.in_width(32), .out_width(24)) bit_extender_5 (.in(alu_1_out_4), .out(bit_extender_5_out));
  RAM #(.addrWidth(24), .dataWidth(32), .bus("separate")) ram_2 (
    .addr(bit_extender_5_out), .din(register_memory_1_busa), .data(ram_2_data), .str(cu_1_memwrite),
    .sel(1'b1), .clk(CLK), .ld(cu_1_memread), .clr(Reset));

  // Notes on the sheet:
  //   Branch
endmodule

module Instruction_Decoder (
  input  [31:0] Inst,
  output [5:0] Opcode,
  output [4:0] rs,
  output [4:0] rt,
  output [4:0] rd,
  output [4:0] shamt,
  output [5:0] funct,
  output [15:0] Immediate,
  output [25:0] address
);


  assign address = Inst[25:0];
  assign funct = Inst[5:0];
  assign Immediate = Inst[15:0];
  assign Opcode = Inst[31:26];
  assign rd = Inst[15:11];
  assign rs = Inst[25:21];
  assign rt = Inst[20:16];
  assign shamt = Inst[10:6];
endmodule

module CU (
  input  [5:0] Opcode,
  output Jump,
  output RegDst,
  output ALUSrc,
  output MemToReg,
  output RegWrite,
  output MemRead,
  output MemWrite,
  output Branch,
  output [1:0] ALUOp,
  output [9:0] DataBus
);

  wire comparator_1_eq, comparator_2_eq, comparator_3_eq, comparator_4_eq, comparator_5_eq, comparator_6_eq;

  Comparator #(.width(6)) comparator_1 (.a(Opcode), .b({6{1'b0}}), .eq(comparator_1_eq));  // open: gt, lt
  Comparator #(.width(6)) comparator_2 (.a(Opcode), .b(6'b001000), .eq(comparator_2_eq));  // open: gt, lt
  Comparator #(.width(6)) comparator_3 (.a(Opcode), .b(6'b100011), .eq(comparator_3_eq));  // open: gt, lt
  Comparator #(.width(6)) comparator_4 (.a(Opcode), .b(6'b101011), .eq(comparator_4_eq));  // open: gt, lt
  Comparator #(.width(6)) comparator_5 (.a(Opcode), .b(6'b000100), .eq(comparator_5_eq));  // open: gt, lt
  Comparator #(.width(6)) comparator_6 (.a(Opcode), .b(6'b000010), .eq(comparator_6_eq));  // open: gt, lt
  assign {DataBus[9:8], ALUSrc, DataBus[6:3], Branch, ALUOp} = comparator_1_eq ? 10'h122 : 10'bz;  // Controlled_Buffer controlled_buffer_1
  assign {DataBus[9:8], ALUSrc, DataBus[6:3], Branch, ALUOp} = comparator_2_eq ? 10'ha0 : 10'bz;  // Controlled_Buffer controlled_buffer_2
  assign {DataBus[9:8], ALUSrc, DataBus[6:3], Branch, ALUOp} = comparator_3_eq ? 10'hf0 : 10'bz;  // Controlled_Buffer controlled_buffer_3
  assign {DataBus[9:8], ALUSrc, DataBus[6:3], Branch, ALUOp} = comparator_4_eq ? 10'h88 : 10'bz;  // Controlled_Buffer controlled_buffer_4
  assign {DataBus[9:8], ALUSrc, DataBus[6:3], Branch, ALUOp} = comparator_5_eq ? 10'h5 : 10'bz;  // Controlled_Buffer controlled_buffer_5
  assign {DataBus[9:8], ALUSrc, DataBus[6:3], Branch, ALUOp} = comparator_6_eq ? 10'h200 : 10'bz;  // Controlled_Buffer controlled_buffer_6

  assign {DataBus[7], DataBus[2:0]} = {ALUSrc, Branch, ALUOp};
  assign Jump = DataBus[9];
  assign MemRead = DataBus[4];
  assign MemToReg = DataBus[6];
  assign MemWrite = DataBus[3];
  assign RegDst = DataBus[8];
  assign RegWrite = DataBus[5];

  // Notes on the sheet:
  //   R-Type
  //   Addi
  //   Load
  //   Store
  //   Branch
  //   Jump
endmodule

module Debug_Circuit (
  input  [5:0] Funct,
  input  [5:0] Opcode,
  input  [25:0] Inst,
  output [5:0] inst3,
  output [5:0] inst2,
  output [5:0] inst1,
  output [5:0] inst0,
  output [5:0] disp0,
  output [5:0] disp1,
  output [5:0] disp2,
  output [5:0] disp3,
  output [5:0] disp4,
  output [5:0] disp5,
  output [5:0] disp6,
  output [5:0] disp7,
  output [5:0] disp8,
  output [5:0] disp9,
  output [5:0] disp10,
  output [5:0] disp11,
  output [5:0] disp12
);

  wire and_1_out, and_2_out, comparator_1_eq, comparator_2_eq, not_1_out, not_2_out, not_3_out;
  wire [9:0] func_parser_1_add;
  wire [31:6] controlled_buffer_1_out;

  Comparator #(.width(6), .mode("unsigned")) comparator_1 (
    .a({6{1'b0}}), .b(Opcode), .eq(comparator_1_eq));  // open: gt, lt
  not not_1 (not_1_out, comparator_1_eq);
  Comparator #(.width(6)) comparator_2 (.a(Opcode), .b(6'b000010), .eq(comparator_2_eq));  // open: gt, lt
  func_parser func_parser_1 (
    .in_1(Funct), .Enable(comparator_1_eq), .add(func_parser_1_add[0]), .subs(func_parser_1_add[1]),
    .\and (func_parser_1_add[2]), .\or (func_parser_1_add[3]), .less_than(func_parser_1_add[4]));
  opcode_parser opcode_parser_1 (
    .in_1(Opcode), .Enable(not_1_out), .addi(func_parser_1_add[5]), .load(func_parser_1_add[6]),
    .store(func_parser_1_add[7]), .branch(func_parser_1_add[8]), .jump(func_parser_1_add[9]));
  not not_2 (not_2_out, comparator_1_eq);
  assign {controlled_buffer_1_out[31:30], inst0, controlled_buffer_1_out[23:22], inst1, controlled_buffer_1_out[15:14], inst2, controlled_buffer_1_out[7:6], inst3} = func_parser_1_add[5] ? 32'h1040409 : 32'bz;  // Controlled_Buffer controlled_buffer_1
  assign {controlled_buffer_1_out[31:30], inst0, controlled_buffer_1_out[23:22], inst1, controlled_buffer_1_out[15:14], inst2, controlled_buffer_1_out[7:6], inst3} = func_parser_1_add[6] ? 32'hc170000 : 32'bz;  // Controlled_Buffer controlled_buffer_2
  assign {controlled_buffer_1_out[31:30], inst0, controlled_buffer_1_out[23:22], inst1, controlled_buffer_1_out[15:14], inst2, controlled_buffer_1_out[7:6], inst3} = func_parser_1_add[7] ? 32'h13170000 : 32'bz;  // Controlled_Buffer controlled_buffer_3
  assign {controlled_buffer_1_out[31:30], inst0, controlled_buffer_1_out[23:22], inst1, controlled_buffer_1_out[15:14], inst2, controlled_buffer_1_out[7:6], inst3} = func_parser_1_add[8] ? 32'h2051100 : 32'bz;  // Controlled_Buffer controlled_buffer_4
  assign {controlled_buffer_1_out[31:30], inst0, controlled_buffer_1_out[23:22], inst1, controlled_buffer_1_out[15:14], inst2, controlled_buffer_1_out[7:6], inst3} = func_parser_1_add[9] ? 32'ha000000 : 32'bz;  // Controlled_Buffer controlled_buffer_5
  assign {controlled_buffer_1_out[31:30], inst0, controlled_buffer_1_out[23:22], inst1, controlled_buffer_1_out[15:14], inst2, controlled_buffer_1_out[7:6], inst3} = func_parser_1_add[0] ? 32'h1040400 : 32'bz;  // Controlled_Buffer controlled_buffer_6
  assign {controlled_buffer_1_out[31:30], inst0, controlled_buffer_1_out[23:22], inst1, controlled_buffer_1_out[15:14], inst2, controlled_buffer_1_out[7:6], inst3} = func_parser_1_add[1] ? 32'h13150200 : 32'bz;  // Controlled_Buffer controlled_buffer_7
  assign {controlled_buffer_1_out[31:30], inst0, controlled_buffer_1_out[23:22], inst1, controlled_buffer_1_out[15:14], inst2, controlled_buffer_1_out[7:6], inst3} = func_parser_1_add[2] ? 32'h10e0400 : 32'bz;  // Controlled_Buffer controlled_buffer_8
  assign {controlled_buffer_1_out[31:30], inst0, controlled_buffer_1_out[23:22], inst1, controlled_buffer_1_out[15:14], inst2, controlled_buffer_1_out[7:6], inst3} = func_parser_1_add[3] ? 32'hf120000 : 32'bz;  // Controlled_Buffer controlled_buffer_9
  assign {controlled_buffer_1_out[31:30], inst0, controlled_buffer_1_out[23:22], inst1, controlled_buffer_1_out[15:14], inst2, controlled_buffer_1_out[7:6], inst3} = func_parser_1_add[4] ? 32'h130c1400 : 32'bz;  // Controlled_Buffer controlled_buffer_10
  Jump_Parser jump_parser_1 (
    .in_1(Inst), .select(comparator_2_eq), .char0(disp6), .char1(disp5), .char2(disp4), .char3(disp3),
    .char4(disp2), .char5(disp1), .char6(disp0));
  and and_1 (and_1_out, not_2_out, ~comparator_2_eq);  // AND_Gate
  assign disp7 = comparator_2_eq ? {6{1'b0}} : 6'bz;  // Controlled_Buffer controlled_buffer_11
  assign disp8 = comparator_2_eq ? {6{1'b0}} : 6'bz;  // Controlled_Buffer controlled_buffer_12
  and and_2 (and_2_out, ~func_parser_1_add[0], ~func_parser_1_add[1], ~func_parser_1_add[2], ~func_parser_1_add[3], ~func_parser_1_add[4], ~func_parser_1_add[5], ~func_parser_1_add[6], ~func_parser_1_add[7], ~func_parser_1_add[8], ~func_parser_1_add[9]);  // AND_Gate
  Immediate_parser immediate_parser_1 (
    .Opcode(Opcode), .Inst(Inst), .select(and_1_out), .sect0({disp3, disp2, disp1, disp0}),
    .sect1({disp7, disp6, disp5, disp4}), .sect2({disp11, disp10, disp9, disp8}), .sect4(disp12));
  assign disp9 = comparator_2_eq ? {6{1'b0}} : 6'bz;  // Controlled_Buffer controlled_buffer_13
  assign disp10 = comparator_2_eq ? {6{1'b0}} : 6'bz;  // Controlled_Buffer controlled_buffer_14
  assign disp11 = comparator_2_eq ? {6{1'b0}} : 6'bz;  // Controlled_Buffer controlled_buffer_15
  assign disp12 = comparator_2_eq ? {6{1'b0}} : 6'bz;  // Controlled_Buffer controlled_buffer_16
  assign {controlled_buffer_1_out[31:30], inst0, controlled_buffer_1_out[23:22], inst1, controlled_buffer_1_out[15:14], inst2, controlled_buffer_1_out[7:6], inst3} = and_2_out ? 32'he0f1000 : 32'bz;  // Controlled_Buffer controlled_buffer_17
  // Probe on Inst[15:11]
  Register_parser register_parser_1 (
    .\reg (Inst[15:11]), .ch2(disp2), .ch1(disp1), .ch0(disp0), .select(comparator_1_eq),
    .comma(comparator_1_eq), .ch3(disp3));
  Register_parser register_parser_2 (
    .\reg (Inst[25:21]), .ch2(disp6), .ch1(disp5), .ch0(disp4), .select(comparator_1_eq),
    .comma(comparator_1_eq), .ch3(disp7));
  // Probe on Inst[20:16]
  Register_parser register_parser_3 (
    .\reg (Inst[20:16]), .ch2(disp10), .ch1(disp9), .ch0(disp8), .select(comparator_1_eq), .comma(not_3_out),
    .ch3(disp11));
  not not_3 (not_3_out, comparator_1_eq);
  assign disp12 = comparator_1_eq ? {6{1'b0}} : 6'bz;  // Controlled_Buffer controlled_buffer_18
endmodule

module func_parser (
  input  [5:0] in_1,
  input  Enable,
  output add,
  output subs,
  output \and ,
  output \or ,
  output less_than
);

  wire comparator_1_eq, comparator_2_eq, comparator_3_eq, comparator_4_eq, comparator_5_eq;

  Comparator #(.width(6)) comparator_1 (.a(in_1), .b(6'b100000), .eq(comparator_1_eq));  // open: gt, lt
  Comparator #(.width(6)) comparator_2 (.a(in_1), .b(6'b100010), .eq(comparator_2_eq));  // open: gt, lt
  Comparator #(.width(6)) comparator_3 (.a(in_1), .b(6'b100100), .eq(comparator_3_eq));  // open: gt, lt
  Comparator #(.width(6)) comparator_4 (.a(in_1), .b(6'b100101), .eq(comparator_4_eq));  // open: gt, lt
  Comparator #(.width(6)) comparator_5 (.a(in_1), .b(6'b101010), .eq(comparator_5_eq));  // open: gt, lt
  and and_1 (add, comparator_1_eq, Enable);
  and and_2 (subs, comparator_2_eq, Enable);
  and and_3 (\and , comparator_3_eq, Enable);
  and and_4 (\or , comparator_4_eq, Enable);
  and and_5 (less_than, comparator_5_eq, Enable);
endmodule

module opcode_parser (
  input  [5:0] in_1,
  input  Enable,
  output addi,
  output load,
  output store,
  output branch,
  output jump
);

  wire and_1_out, and_2_out, and_3_out, and_4_out, and_5_out, not_1_out, not_2_out, not_3_out, not_4_out,
       not_5_out, not_6_out, not_7_out, not_8_out, not_9_out, not_10_out, not_11_out, not_12_out, not_13_out,
       not_14_out, not_15_out, not_16_out, not_17_out, not_18_out, not_19_out, not_20_out;

  not not_1 (not_1_out, in_1[5]);
  not not_2 (not_2_out, in_1[4]);
  not not_3 (not_3_out, in_1[2]);
  not not_4 (not_4_out, in_1[1]);
  not not_5 (not_5_out, in_1[0]);
  not not_6 (not_6_out, in_1[4]);
  not not_7 (not_7_out, in_1[3]);
  not not_8 (not_8_out, in_1[2]);
  not not_9 (not_9_out, in_1[4]);
  not not_10 (not_10_out, in_1[2]);
  not not_11 (not_11_out, in_1[5]);
  not not_12 (not_12_out, in_1[4]);
  not not_13 (not_13_out, in_1[3]);
  not not_14 (not_14_out, in_1[1]);
  not not_15 (not_15_out, in_1[0]);
  not not_16 (not_16_out, in_1[5]);
  not not_17 (not_17_out, in_1[4]);
  not not_18 (not_18_out, in_1[3]);
  not not_19 (not_19_out, in_1[2]);
  not not_20 (not_20_out, in_1[0]);
  and and_1 (and_1_out, not_1_out, not_2_out, in_1[3], not_3_out, not_4_out, not_5_out);
  and and_2 (and_2_out, in_1[5], not_6_out, not_7_out, not_8_out, in_1[1], in_1[0]);
  and and_3 (and_3_out, in_1[5], not_9_out, in_1[3], not_10_out, in_1[1], in_1[0]);
  and and_4 (and_4_out, not_11_out, not_12_out, not_13_out, in_1[2], not_14_out, not_15_out);
  and and_5 (and_5_out, not_16_out, not_17_out, not_18_out, not_19_out, in_1[1], not_20_out);
  and and_6 (addi, and_1_out, Enable);
  and and_7 (load, and_2_out, Enable);
  and and_8 (store, and_3_out, Enable);
  buf and_9 (branch, and_4_out);  // AND_Gate
  and and_10 (jump, and_5_out, Enable);
endmodule

module Display_Driver (
  input  [5:0] in_1,
  output [6:0] col0,
  output [6:0] col1,
  output [6:0] col2,
  output [6:0] col3,
  output [6:0] col4
);

  wire [15:7] rom_2_data;
  wire [19:3] rom_1_data;

  ROM #(.addrWidth(6), .dataWidth(20)) rom_1 (
    .addr(in_1), .data({rom_1_data[19], col0, rom_1_data[11], col1, rom_1_data[3], col2[6:4]}));  // open: sel
  ROM #(.addrWidth(6), .dataWidth(20)) rom_2 (
    .addr(in_1), .data({col2[3:0], rom_2_data[15], col3, rom_2_data[7], col4}));  // open: sel
  DotMatrix dotmatrix_1 (.col0(col0), .col1(col1), .col2(col2), .col3(col3), .col4(col4));

  // Notes on the sheet:
  //   contents of rom_1 (hex, n*v repeats v):
  //   0 3f444 7f494 3e414 7f414 7f494 7f484 3e414 7f080 41417 46414 7f080 7f010 7f201 7f201 3e414 7f484
  //   3e414 7f444 31494 40407 7e010 7c020 7f020 63140 70080 43454 3e454 417 27494 22414 78080 79494 3e494
  //   40474 36494 32494 122a7 50 3 41413
  //   contents of rom_2 (hex, n*v repeats v):
  //   0 4443f 94936 14122 1413e 94949 84040 9492e 8087f f4141 17e40 81463 10101 8207f 87f 1413e 84830
  //   3413e 4443b 94946 f4040 1017e 1027c c027f 81463 70870 95161 9513e f0100 94931 94936 87f08 94946
  //   94906 84870 94936 9493e f2a24 60000 e4141 e0000
endmodule

module ALU_Control (
  input  [1:0] ALUOp,
  input  [5:0] Funct,
  output [3:0] Operation
);

  wire and_1_out, and_2_out, and_3_out, comparator_1_eq, comparator_2_eq, comparator_3_eq, comparator_4_eq,
       comparator_5_eq, or_1_out;
  wire [3:0] bit_extender_1_out;

  Bit_Extender #(.in_width(6), .out_width(4)) bit_extender_1 (.in(Funct), .out(bit_extender_1_out));
  and and_1 (and_1_out, ~ALUOp[0], ~ALUOp[1]);  // AND_Gate
  Comparator #(.width(4)) comparator_1 (.a(bit_extender_1_out), .b(4'b0000), .eq(comparator_1_eq));  // open: gt, lt
  Comparator #(.width(4)) comparator_2 (.a(bit_extender_1_out), .b(4'b0010), .eq(comparator_2_eq));  // open: gt, lt
  Comparator #(.width(4)) comparator_3 (.a(bit_extender_1_out), .b(4'b0100), .eq(comparator_3_eq));  // open: gt, lt
  Comparator #(.width(4)) comparator_4 (.a(bit_extender_1_out), .b(4'b0101), .eq(comparator_4_eq));  // open: gt, lt
  Comparator #(.width(4)) comparator_5 (.a(bit_extender_1_out), .b(4'b1010), .eq(comparator_5_eq));  // open: gt, lt
  and and_2 (and_2_out, ~and_1_out, ALUOp[0]);  // AND_Gate
  assign and_2_out = ALUOp[1] ? comparator_2_eq : 1'bz;  // Controlled_Buffer controlled_buffer_1
  and and_3 (and_3_out, comparator_3_eq, ALUOp[1]);
  or or_1 (or_1_out, and_1_out, comparator_1_eq);
  assign Operation = or_1_out ? 4'b0010 : 4'bz;  // Controlled_Buffer controlled_buffer_2
  assign Operation = and_2_out ? 4'b0110 : 4'bz;  // Controlled_Buffer controlled_buffer_3
  assign Operation = and_3_out ? 4'b0000 : 4'bz;  // Controlled_Buffer controlled_buffer_4
  assign Operation = comparator_4_eq ? 4'b0001 : 4'bz;  // Controlled_Buffer controlled_buffer_5
  assign Operation = comparator_5_eq ? 4'b0111 : 4'bz;  // Controlled_Buffer controlled_buffer_6

  // Notes on the sheet:
  //   Suma
  //   Resta
  //   And
  //   Or
  //   Less Than
endmodule

module Register_parser (
  input  [4:0] \reg ,
  input  select,
  input  comma,
  output [5:0] ch3,
  output [5:0] ch2,
  output [5:0] ch1,
  output [5:0] ch0
);

  wire and_1_out, not_1_out, not_2_out;
  wire [5:0] controlled_buffer_1_out, controlled_buffer_3_out;
  wire [15:0] multiplexer_1_out;

  Multiplexer #(.select(5), .width(16), .disabled(0)) multiplexer_1 (
    .in0(16'h1a12), .in1(16'h114), .in2(16'h161b), .in3(16'h161c), .in4(16'h11b), .in5(16'h11c),
    .in6(16'h11d), .in7(16'h11e), .in8(16'h141b), .in9(16'h141c), .in10(16'h141d), .in11(16'h141e),
    .in12(16'h141f), .in13(16'h1420), .in14(16'h1421), .in15(16'h1422), .in16(16'h131b), .in17(16'h131c),
    .in18(16'h131d), .in19(16'h131e), .in20(16'h131f), .in21(16'h1320), .in22(16'h1321), .in23(16'h1322),
    .in24(16'h1423), .in25(16'h1424), .in26(16'hb1b), .in27(16'hb1c), .in28(16'h710), .in29(16'h1310),
    .in30(16'h610), .in31(16'h1201), .out(multiplexer_1_out), .sel(\reg ), .en(select));
  not not_1 (not_1_out, and_1_out);
  not not_2 (not_2_out, select);
  and and_1 (and_1_out, comma, select);
  assign controlled_buffer_1_out = not_1_out ? {6{1'b0}} : 6'bz;  // Controlled_Buffer controlled_buffer_1
  assign controlled_buffer_1_out = and_1_out ? 6'b100110 : 6'bz;  // Controlled_Buffer controlled_buffer_2
  assign controlled_buffer_3_out = not_2_out ? {6{1'b0}} : 6'bz;  // Controlled_Buffer controlled_buffer_3
  assign controlled_buffer_3_out = select ? 6'b100101 : 6'bz;  // Controlled_Buffer controlled_buffer_4
  assign ch1 = select ? multiplexer_1_out[13:8] : 6'bz;  // Controlled_Buffer controlled_buffer_5
  assign ch0 = select ? controlled_buffer_3_out : 6'bz;  // Controlled_Buffer controlled_buffer_6
  assign ch3 = select ? controlled_buffer_1_out : 6'bz;  // Controlled_Buffer controlled_buffer_7
  assign ch2 = select ? multiplexer_1_out[5:0] : 6'bz;  // Controlled_Buffer controlled_buffer_8
endmodule

module Immediate_parser (
  input  [5:0] Opcode,
  input  [25:0] Inst,
  input  select,
  output [23:0] sect0,
  output [23:0] sect1,
  output [23:0] sect2,
  output [5:0] sect4
);

  wire comparator_1_eq, comparator_1_gt, comparator_1_lt, not_1_out, or_1_out;
  wire [5:0] controlled_buffer_1_out, controlled_buffer_5_out, hex_parser_1_out_2, hex_parser_2_out_2,
       hex_parser_3_out_2, hex_parser_4_out_2, hex_parser_5_out_2, hex_parser_6_out_2, hex_parser_7_out_2,
       hex_parser_8_out_2, register_parser_2_ch1, register_parser_2_ch3, register_parser_4_ch0,
       register_parser_4_ch1, register_parser_4_ch2;
  wire [17:0] register_parser_2_ch0;
  wire [23:0] register_parser_1_ch0;

  // Probe on Inst
  Comparator #(.width(6), .mode("unsigned")) comparator_1 (
    .a(Opcode), .b(6'b001000), .gt(comparator_1_gt), .eq(comparator_1_eq), .lt(comparator_1_lt));
  or or_1 (or_1_out, comparator_1_eq, comparator_1_lt);
  Register_parser register_parser_1 (
    .\reg (Inst[20:16]), .ch2(register_parser_1_ch0[17:12]), .ch1(register_parser_1_ch0[11:6]),
    .ch0(register_parser_1_ch0[5:0]), .select(or_1_out), .comma(or_1_out), .ch3(register_parser_1_ch0[23:18]));
  Register_parser register_parser_2 (
    .\reg (Inst[25:21]), .ch2(register_parser_2_ch0[17:12]), .ch1(register_parser_2_ch1),
    .ch0(register_parser_2_ch0[5:0]), .select(or_1_out), .comma(or_1_out), .ch3(register_parser_2_ch3));
  Register_parser register_parser_3 (
    .\reg (Inst[20:16]), .ch2(register_parser_1_ch0[17:12]), .ch1(register_parser_1_ch0[11:6]),
    .ch0(register_parser_1_ch0[5:0]), .select(comparator_1_gt), .comma(comparator_1_gt),
    .ch3(register_parser_1_ch0[23:18]));
  Register_parser register_parser_4 (
    .\reg (Inst[25:21]), .ch2(register_parser_4_ch2), .ch1(register_parser_4_ch1),
    .ch0(register_parser_4_ch0), .select(comparator_1_gt), .comma(not_1_out));  // open: ch3
  not not_1 (not_1_out, comparator_1_gt);
  Hex_parser hex_parser_1 (.in_1(Inst[15:12]), .out_2(hex_parser_1_out_2));
  Hex_parser hex_parser_2 (.in_1(Inst[11:8]), .out_2(hex_parser_2_out_2));
  Hex_parser hex_parser_3 (.in_1(Inst[7:4]), .out_2(hex_parser_3_out_2));
  Hex_parser hex_parser_4 (.in_1(Inst[3:0]), .out_2(hex_parser_4_out_2));
  Hex_parser hex_parser_5 (.in_1(Inst[15:12]), .out_2(hex_parser_5_out_2));
  Hex_parser hex_parser_6 (.in_1(Inst[11:8]), .out_2(hex_parser_6_out_2));
  Hex_parser hex_parser_7 (.in_1(Inst[7:4]), .out_2(hex_parser_7_out_2));
  Hex_parser hex_parser_8 (.in_1(Inst[3:0]), .out_2(hex_parser_8_out_2));
  assign controlled_buffer_1_out = or_1_out ? hex_parser_1_out_2 : 6'bz;  // Controlled_Buffer controlled_buffer_1
  assign register_parser_4_ch0 = or_1_out ? hex_parser_2_out_2 : 6'bz;  // Controlled_Buffer controlled_buffer_2
  assign register_parser_4_ch1 = or_1_out ? hex_parser_3_out_2 : 6'bz;  // Controlled_Buffer controlled_buffer_3
  assign register_parser_4_ch2 = or_1_out ? hex_parser_4_out_2 : 6'bz;  // Controlled_Buffer controlled_buffer_4
  assign controlled_buffer_5_out = or_1_out ? {6{1'b0}} : 6'bz;  // Controlled_Buffer controlled_buffer_5
  assign register_parser_2_ch0[5:0] = comparator_1_gt ? hex_parser_5_out_2 : 6'bz;  // Controlled_Buffer controlled_buffer_6
  assign register_parser_2_ch1 = comparator_1_gt ? hex_parser_6_out_2 : 6'bz;  // Controlled_Buffer controlled_buffer_7
  assign register_parser_2_ch0[17:12] = comparator_1_gt ? hex_parser_7_out_2 : 6'bz;  // Controlled_Buffer controlled_buffer_8
  assign register_parser_2_ch3 = comparator_1_gt ? hex_parser_8_out_2 : 6'bz;  // Controlled_Buffer controlled_buffer_9
  assign controlled_buffer_5_out = comparator_1_gt ? 6'b101000 : 6'bz;  // Controlled_Buffer controlled_buffer_10
  assign controlled_buffer_1_out = comparator_1_gt ? 6'b100111 : 6'bz;  // Controlled_Buffer controlled_buffer_11
  assign sect0 = select ? register_parser_1_ch0 : 24'bz;  // Controlled_Buffer controlled_buffer_12
  assign sect1 = select ? {register_parser_2_ch3, register_parser_2_ch0[17:12], register_parser_2_ch1, register_parser_2_ch0[5:0]} : 24'bz;  // Controlled_Buffer controlled_buffer_13
  assign sect2 = select ? {register_parser_4_ch2, register_parser_4_ch1, register_parser_4_ch0, controlled_buffer_1_out} : 24'bz;  // Controlled_Buffer controlled_buffer_14
  assign sect4 = select ? controlled_buffer_5_out : 6'bz;  // Controlled_Buffer controlled_buffer_15
endmodule

module Hex_parser (
  input  [3:0] in_1,
  output [5:0] out_2
);

  wire comparator_1_gt, not_1_out;
  wire [5:0] adder_1_out, bit_extender_1_out, subtractor_1_out;

  assign bit_extender_1_out = {{2{1'b0}}, in_1};  // Bit_Extender bit_extender_1
  Comparator #(.width(6)) comparator_1 (.a(bit_extender_1_out), .b(6'b001001), .gt(comparator_1_gt));  // open: eq, lt
  not not_1 (not_1_out, comparator_1_gt);
  Adder #(.width(6)) adder_1 (.a(bit_extender_1_out), .b(6'b011011), .out(adder_1_out));  // open: cin, cout
  Subtractor #(.width(6)) subtractor_1 (
    .a(bit_extender_1_out), .b(6'b001001), .out(subtractor_1_out));  // open: bin, bout
  assign out_2 = not_1_out ? adder_1_out : 6'bz;  // Controlled_Buffer controlled_buffer_1
  assign out_2 = comparator_1_gt ? subtractor_1_out : 6'bz;  // Controlled_Buffer controlled_buffer_2
endmodule

module Jump_Parser (
  input  [25:0] in_1,
  input  select,
  output [5:0] char0,
  output [5:0] char1,
  output [5:0] char2,
  output [5:0] char3,
  output [5:0] char4,
  output [5:0] char5,
  output [5:0] char6
);

  wire [5:0] hex_parser_1_out_2, hex_parser_2_out_2, hex_parser_3_out_2, hex_parser_4_out_2,
       hex_parser_5_out_2, hex_parser_6_out_2, hex_parser_7_out_2;

  Hex_parser hex_parser_1 (.in_1(in_1[3:0]), .out_2(hex_parser_1_out_2));
  Hex_parser hex_parser_2 (.in_1(in_1[7:4]), .out_2(hex_parser_2_out_2));
  Hex_parser hex_parser_3 (.in_1(in_1[11:8]), .out_2(hex_parser_3_out_2));
  Hex_parser hex_parser_4 (.in_1(in_1[15:12]), .out_2(hex_parser_4_out_2));
  Hex_parser hex_parser_5 (.in_1(in_1[19:16]), .out_2(hex_parser_5_out_2));
  Hex_parser hex_parser_6 (.in_1(in_1[23:20]), .out_2(hex_parser_6_out_2));
  Hex_parser hex_parser_7 (.in_1({2'b00, in_1[25:24]}), .out_2(hex_parser_7_out_2));
  assign char0 = select ? hex_parser_1_out_2 : 6'bz;  // Controlled_Buffer controlled_buffer_1
  assign char1 = select ? hex_parser_2_out_2 : 6'bz;  // Controlled_Buffer controlled_buffer_2
  assign char2 = select ? hex_parser_3_out_2 : 6'bz;  // Controlled_Buffer controlled_buffer_3
  assign char3 = select ? hex_parser_4_out_2 : 6'bz;  // Controlled_Buffer controlled_buffer_4
  assign char4 = select ? hex_parser_5_out_2 : 6'bz;  // Controlled_Buffer controlled_buffer_5
  assign char5 = select ? hex_parser_6_out_2 : 6'bz;  // Controlled_Buffer controlled_buffer_6
  assign char6 = select ? hex_parser_7_out_2 : 6'bz;  // Controlled_Buffer controlled_buffer_7
endmodule

module Register_Memory (
  input  Write_Enable,
  input  [31:0] Data_in,
  input  Clk,
  input  Clear_Reset,
  input  [4:0] regA,
  input  [4:0] RegB,
  input  [4:0] RegC,
  output [31:0] BusB,
  output [31:0] BusA
);

  wire demultiplexer_1_out0, demultiplexer_1_out1, demultiplexer_1_out2, demultiplexer_1_out3,
       demultiplexer_1_out4, demultiplexer_1_out5, demultiplexer_1_out6, demultiplexer_1_out7,
       demultiplexer_1_out8, demultiplexer_1_out9, demultiplexer_1_out10, demultiplexer_1_out11,
       demultiplexer_1_out12, demultiplexer_1_out13, demultiplexer_1_out14, demultiplexer_1_out15,
       demultiplexer_1_out16, demultiplexer_1_out17, demultiplexer_1_out18, demultiplexer_1_out19,
       demultiplexer_1_out20, demultiplexer_1_out21, demultiplexer_1_out22, demultiplexer_1_out23,
       demultiplexer_1_out24, demultiplexer_1_out25, demultiplexer_1_out26, demultiplexer_1_out27,
       demultiplexer_1_out28, demultiplexer_1_out29, demultiplexer_1_out30, demultiplexer_1_out31;
  wire [31:0] a0_q, a1_q, a2_q, a3_q, at_q, fp_q, gp_q, k0_q, k1_q, ra_q, s0_q, s1_q, s2_q, s3_q, s4_q, s5_q,
       s6_q, s7_q, sp_q, t0_q, t1_q, t2_q, t3_q, t4_q, t5_q, t6_q, t7_q, t8_q, t9_q, v0_q, v1_q, zero_q;

  Register #(.width(32)) zero (.D(Data_in), .en(demultiplexer_1_out0), .Q(zero_q), .clk(Clk), .clr(Clear_Reset));
  Register #(.width(32)) at (.D(Data_in), .en(demultiplexer_1_out1), .Q(at_q), .clk(Clk), .clr(Clear_Reset));
  Register #(.width(32)) v0 (.D(Data_in), .en(demultiplexer_1_out2), .Q(v0_q), .clk(Clk), .clr(Clear_Reset));
  Register #(.width(32)) v1 (.D(Data_in), .en(demultiplexer_1_out3), .Q(v1_q), .clk(Clk), .clr(Clear_Reset));
  Register #(.width(32)) a0 (.D(Data_in), .en(demultiplexer_1_out4), .Q(a0_q), .clk(Clk), .clr(Clear_Reset));
  Register #(.width(32)) a1 (.D(Data_in), .en(demultiplexer_1_out5), .Q(a1_q), .clk(Clk), .clr(Clear_Reset));
  Register #(.width(32)) a2 (.D(Data_in), .en(demultiplexer_1_out6), .Q(a2_q), .clk(Clk), .clr(Clear_Reset));
  Register #(.width(32)) a3 (.D(Data_in), .en(demultiplexer_1_out7), .Q(a3_q), .clk(Clk), .clr(Clear_Reset));
  Register #(.width(32)) t0 (.D(Data_in), .en(demultiplexer_1_out8), .Q(t0_q), .clk(Clk), .clr(Clear_Reset));
  Register #(.width(32)) t1 (.D(Data_in), .en(demultiplexer_1_out9), .Q(t1_q), .clk(Clk), .clr(Clear_Reset));
  Register #(.width(32)) t2 (.D(Data_in), .en(demultiplexer_1_out10), .Q(t2_q), .clk(Clk), .clr(Clear_Reset));
  Register #(.width(32)) t3 (.D(Data_in), .en(demultiplexer_1_out11), .Q(t3_q), .clk(Clk), .clr(Clear_Reset));
  Demultiplexer #(.select(5), .enable("false")) demultiplexer_1 (
    .out0(demultiplexer_1_out0), .out1(demultiplexer_1_out1), .out2(demultiplexer_1_out2),
    .out3(demultiplexer_1_out3), .out4(demultiplexer_1_out4), .out5(demultiplexer_1_out5),
    .out6(demultiplexer_1_out6), .out7(demultiplexer_1_out7), .out8(demultiplexer_1_out8),
    .out9(demultiplexer_1_out9), .out10(demultiplexer_1_out10), .out11(demultiplexer_1_out11),
    .out12(demultiplexer_1_out12), .out13(demultiplexer_1_out13), .out14(demultiplexer_1_out14),
    .out15(demultiplexer_1_out15), .out16(demultiplexer_1_out16), .out17(demultiplexer_1_out17),
    .out18(demultiplexer_1_out18), .out19(demultiplexer_1_out19), .out20(demultiplexer_1_out20),
    .out21(demultiplexer_1_out21), .out22(demultiplexer_1_out22), .out23(demultiplexer_1_out23),
    .out24(demultiplexer_1_out24), .out25(demultiplexer_1_out25), .out26(demultiplexer_1_out26),
    .out27(demultiplexer_1_out27), .out28(demultiplexer_1_out28), .out29(demultiplexer_1_out29),
    .out30(demultiplexer_1_out30), .out31(demultiplexer_1_out31), .in(Write_Enable), .sel(RegC));
  Register #(.width(32)) t4 (.D(Data_in), .en(demultiplexer_1_out12), .Q(t4_q), .clk(Clk), .clr(Clear_Reset));
  Register #(.width(32)) t5 (.D(Data_in), .en(demultiplexer_1_out13), .Q(t5_q), .clk(Clk), .clr(Clear_Reset));
  Register #(.width(32)) t6 (.D(Data_in), .en(demultiplexer_1_out14), .Q(t6_q), .clk(Clk), .clr(Clear_Reset));
  Register #(.width(32)) t7 (.D(Data_in), .en(demultiplexer_1_out15), .Q(t7_q), .clk(Clk), .clr(Clear_Reset));
  Register #(.width(32)) s0 (.D(Data_in), .en(demultiplexer_1_out16), .Q(s0_q), .clk(Clk), .clr(Clear_Reset));
  Register #(.width(32)) s1 (.D(Data_in), .en(demultiplexer_1_out17), .Q(s1_q), .clk(Clk), .clr(Clear_Reset));
  Register #(.width(32)) s2 (.D(Data_in), .en(demultiplexer_1_out18), .Q(s2_q), .clk(Clk), .clr(Clear_Reset));
  Register #(.width(32)) s3 (.D(Data_in), .en(demultiplexer_1_out19), .Q(s3_q), .clk(Clk), .clr(Clear_Reset));
  Register #(.width(32)) s4 (.D(Data_in), .en(demultiplexer_1_out20), .Q(s4_q), .clk(Clk), .clr(Clear_Reset));
  Register #(.width(32)) s5 (.D(Data_in), .en(demultiplexer_1_out21), .Q(s5_q), .clk(Clk), .clr(Clear_Reset));
  Register #(.width(32)) s6 (.D(Data_in), .en(demultiplexer_1_out22), .Q(s6_q), .clk(Clk), .clr(Clear_Reset));
  Register #(.width(32)) s7 (.D(Data_in), .en(demultiplexer_1_out23), .Q(s7_q), .clk(Clk), .clr(Clear_Reset));
  Register #(.width(32)) t8 (.D(Data_in), .en(demultiplexer_1_out24), .Q(t8_q), .clk(Clk), .clr(Clear_Reset));
  Register #(.width(32)) t9 (.D(Data_in), .en(demultiplexer_1_out25), .Q(t9_q), .clk(Clk), .clr(Clear_Reset));
  Register #(.width(32)) k0 (.D(Data_in), .en(demultiplexer_1_out26), .Q(k0_q), .clk(Clk), .clr(Clear_Reset));
  Register #(.width(32)) k1 (.D(Data_in), .en(demultiplexer_1_out27), .Q(k1_q), .clk(Clk), .clr(Clear_Reset));
  Register #(.width(32)) gp (.D(Data_in), .en(demultiplexer_1_out28), .Q(gp_q), .clk(Clk), .clr(Clear_Reset));
  Register #(.width(32)) sp (.D(Data_in), .en(demultiplexer_1_out29), .Q(sp_q), .clk(Clk));  // open: clr
  Register #(.width(32)) fp (.D(Data_in), .en(demultiplexer_1_out30), .Q(fp_q), .clk(Clk), .clr(Clear_Reset));
  Register #(.width(32)) ra (.D(Data_in), .en(demultiplexer_1_out31), .Q(ra_q), .clk(Clk), .clr(Clear_Reset));
  Multiplexer #(.select(5), .width(32)) multiplexer_1 (
    .in0(zero_q), .in1(at_q), .in2(v0_q), .in3(v1_q), .in4(a0_q), .in5(a1_q), .in6(a2_q), .in7(a3_q),
    .in8(t0_q), .in9(t1_q), .in10(t2_q), .in11(t3_q), .in12(t4_q), .in13(t5_q), .in14(t6_q), .in15(t7_q),
    .in16(s0_q), .in17(s1_q), .in18(s2_q), .in19(s3_q), .in20(s4_q), .in21(s5_q), .in22(s6_q), .in23(s7_q),
    .in24(t8_q), .in25(t9_q), .in26(k0_q), .in27(k1_q), .in28(gp_q), .in29(sp_q), .in30(fp_q), .in31(ra_q),
    .out(BusB), .sel(regA));  // open: en
  Multiplexer #(.select(5), .width(32)) multiplexer_2 (
    .in0(zero_q), .in1(at_q), .in2(v0_q), .in3(v1_q), .in4(a0_q), .in5(a1_q), .in6(a2_q), .in7(a3_q),
    .in8(t0_q), .in9(t1_q), .in10(t2_q), .in11(t3_q), .in12(t4_q), .in13(t5_q), .in14(t6_q), .in15(t7_q),
    .in16(s0_q), .in17(s1_q), .in18(s2_q), .in19(s3_q), .in20(s4_q), .in21(s5_q), .in22(s6_q), .in23(s7_q),
    .in24(t8_q), .in25(t9_q), .in26(k0_q), .in27(k1_q), .in28(gp_q), .in29(sp_q), .in30(fp_q), .in31(ra_q),
    .out(BusA), .sel(RegB));  // open: en
endmodule

module ALU (
  input  [31:0] Input_A,
  input  [31:0] Input_B,
  input  [3:0] ALUOp,
  output [31:0] out_4,
  output Zero
);

  wire [31:0] adder_1_out, and_1_out, or_1_out, subtractor_1_out;

  Adder #(.width(32)) adder_1 (.a(Input_A), .b(Input_B), .out(adder_1_out));  // open: cin, cout
  Subtractor #(.width(32)) subtractor_1 (.a(Input_A), .b(Input_B), .out(subtractor_1_out));  // open: bin, bout
  Comparator #(.width(32), .mode("unsigned")) comparator_1 (.a(Input_A), .b(Input_B), .eq(Zero));  // open: gt, lt
  assign and_1_out = Input_A & Input_B;  // AND_Gate and_1, 32 bits wide
  assign or_1_out = Input_A | Input_B;  // OR_Gate or_1, 32 bits wide
  Multiplexer #(.select(4), .width(32), .enable("false")) multiplexer_1 (
    .in0(and_1_out), .in1(or_1_out), .in2(adder_1_out), .in6(subtractor_1_out), .out(out_4), .sel(ALUOp));  // open: in3, in4, in5, in7, in8, in9, in10, in11, in12, in13, in14, in15
endmodule

module IF_ID (
  input  [31:0] \Instrucción ,
  input  [23:0] PC,
  input  in_3,
  input  in_4,
  output [23:0] out_5,
  output [31:0] out_6,
  output [23:0] out_7
);

  wire [23:0] adder_1_out;

  Register #(.width(32)) register_1 (.D(\Instrucción ), .Q(out_6), .clk(in_3), .clr(in_4));  // open: en
  Register #(.width(24)) register_2 (.D(adder_1_out), .Q(out_5), .clk(in_3), .clr(in_4));  // open: en
  Adder #(.width(24)) adder_1 (.a(24'h1), .b(PC), .out(adder_1_out));  // open: cin, cout
  Register #(.width(24)) register_3 (.D(PC), .Q(out_7), .clk(in_3), .clr(in_4));  // open: en
endmodule

module ID_EX (
  input  [23:0] PC___1,
  input  [9:0] Control_Signals,
  input  [15:0] Imm16,
  input  [31:0] BusA,
  input  [31:0] BusB,
  input  [4:0] rt,
  input  [4:0] rd,
  input  CLK,
  input  Rst,
  output [23:0] PC___1_2,
  output RegDst,
  output ALUSrc,
  output [1:0] ALUOp,
  output [5:0] Control_Signals_2,
  output [15:0] Imm16_2,
  output [31:0] BusA_2,
  output [31:0] BusB_2,
  output [4:0] rt_2,
  output [4:0] rd_2
);

  Register #(.width(24)) register_1 (.D(PC___1), .Q(PC___1_2), .clk(CLK), .clr(Rst));  // open: en
  Register #(.width(10)) register_2 (
    .D(Control_Signals), .Q({Control_Signals_2[5], RegDst, ALUSrc, Control_Signals_2[4:0], ALUOp}),
    .clk(CLK), .clr(Rst));  // open: en
  Register #(.width(16)) register_3 (.D(Imm16), .Q(Imm16_2), .clk(CLK), .clr(Rst));  // open: en
  Register #(.width(32)) register_4 (.D(BusA), .Q(BusA_2), .clk(CLK), .clr(Rst));  // open: en
  Register #(.width(32)) register_5 (.D(BusB), .Q(BusB_2), .clk(CLK), .clr(Rst));  // open: en
  Register #(.width(5)) register_6 (.D(rt), .Q(rt_2), .clk(CLK), .clr(Rst));  // open: en
  Register #(.width(5)) register_7 (.D(rd), .Q(rd_2), .clk(CLK), .clr(Rst));  // open: en
endmodule

module EX_MEM (
  input  [23:0] PC___1,
  input  Zero_flag,
  input  [31:0] ALURes,
  input  [31:0] Data_Bus,
  input  [4:0] Reg,
  input  [5:0] Control_Signals,
  input  CLK,
  input  Rst,
  output [23:0] PC___1_2,
  output Zero_flag_2,
  output [31:0] ALURes_2,
  output [31:0] Data_Bus_2,
  output [4:0] Reg_2,
  output Branch,
  output MemWrite,
  output [3:0] Control_Signals_2
);

  Register #(.width(24)) register_1 (.D(PC___1), .Q(PC___1_2), .clk(CLK), .clr(Rst));  // open: en
  Register #(.width(1)) register_2 (.D(Zero_flag), .Q(Zero_flag_2), .clk(CLK), .clr(Rst));  // open: en
  Register #(.width(32)) register_3 (.D(ALURes), .Q(ALURes_2), .clk(CLK), .clr(Rst));  // open: en
  Register #(.width(32)) register_4 (.D(Data_Bus), .Q(Data_Bus_2), .clk(CLK), .clr(Rst));  // open: en
  Register #(.width(5)) register_5 (.D(Reg), .Q(Reg_2), .clk(CLK), .clr(Rst));  // open: en
  Register #(.width(6)) register_6 (
    .D(Control_Signals), .Q({Control_Signals_2, MemWrite, Branch}), .clk(CLK), .clr(Rst));  // open: en
endmodule

module MEM_WR (
  input  [31:0] Data_In,
  input  [31:0] Address,
  input  [4:0] Dest_Reg,
  input  [3:0] Contro_signals,
  input  CLK,
  input  Rst,
  output [31:0] Data_In_2,
  output [31:0] Address_2,
  output [4:0] Dest_Reg_2,
  output MemRead,
  output RegWrite,
  output MemToReg,
  output Jump
);

  Register #(.width(32)) register_1 (.D(Data_In), .Q(Data_In_2), .clk(CLK), .clr(Rst));  // open: en
  Register #(.width(32)) register_2 (.D(Address), .Q(Address_2), .clk(CLK), .clr(Rst));  // open: en
  Register #(.width(5)) register_3 (.D(Dest_Reg), .Q(Dest_Reg_2), .clk(CLK), .clr(Rst));  // open: en
  Register #(.width(4)) register_4 (
    .D(Contro_signals), .Q({Jump, MemToReg, RegWrite, MemRead}), .clk(CLK), .clr(Rst));  // open: en
endmodule
