// Logisim project inst logic.circ as structural Verilog: 4 circuits, main circuit Parser de Inst
module Parser_de_Inst (
  input  [31:0] Inst,
  output [5:0] Opcode,
  output [4:0] Reg1,
  output [4:0] Reg2,
  output [4:0] Destino,
  output [4:0] Shift,
  output [5:0] Funct,
  output [15:0] Imm_Val,
  output [25:0] addr
);


  assign addr = Inst[25:0];
  assign Destino = Inst[15:11];
  assign Funct = Inst[5:0];
  assign Imm_Val = Inst[15:0];
  assign Opcode = Inst[31:26];
  assign Reg1 = Inst[25:21];
  assign Reg2 = Inst[20:16];
  assign Shift = Inst[10:6];
endmodule

module Instruction_Memory (
  input  [23:0] Address,
  input  Chip_Select,
  input  CLK,
  output [31:0] Data
);

  wire not_1_out;

  not not_1 (not_1_out, Chip_Select);
  RAM #(.addrWidth(24), .dataWidth(32)) ram_1 (
    .addr(Address), .data(Data), .sel(not_1_out), .clk(CLK), .ld(1'b1), .clr(1'b0));

  // Notes on the sheet:
  //   Chip_Select: pull=down
endmodule

module PC (
  input  [23:0] Data_In,
  input  CLK,
  input  Clear,
  output [23:0] Data_Out
);

  Register #(.width(24)) register_1 (.D(Data_In), .en(1'b1), .Q(Data_Out), .clk(CLK), .clr(Clear));
endmodule

module inst_addr_display_controller (
  input  [23:0] in_1,
  output [3:0] D5,
  output [3:0] D4,
  output [3:0] D3,
  output [3:0] D2,
  output [3:0] D1,
  output [3:0] D0
);


  assign D0 = in_1[3:0];
  assign D1 = in_1[7:4];
  assign D2 = in_1[11:8];
  assign D3 = in_1[15:12];
  assign D4 = in_1[19:16];
  assign D5 = in_1[23:20];
endmodule
